// Logisim project FullAdder.circ as structural Verilog: 2 circuits, main circuit main
module main (
  input  A,
  input  B,
  input  Cin,
  output S,
  output Cout
);

  wire and_1_out, and_2_out, xor_1_out;

  and and_1 (and_1_out, A, B);
  xor xor_1 (xor_1_out, A, B);
  xor xor_2 (S, xor_1_out, Cin);
  and and_2 (and_2_out, xor_1_out, Cin);
  or or_1 (Cout, and_2_out, and_1_out);
endmodule

module FA4Bit (
  input  [3:0] in_1,
  input  [3:0] in_2,
  input  in_3,
  output [4:0] out_4
);

  wire main_2_cout, main_3_cout, main_4_cout;

  main main_1 (.B(in_2[3]), .Cin(main_2_cout), .A(in_1[3]), .S(out_4[3]), .Cout(out_4[4]));
  main main_2 (.B(in_2[2]), .Cin(main_3_cout), .A(in_1[2]), .S(out_4[2]), .Cout(main_2_cout));
  main main_3 (.B(in_2[1]), .Cin(main_4_cout), .A(in_1[1]), .S(out_4[1]), .Cout(main_3_cout));
  main main_4 (.B(in_2[0]), .Cin(in_3), .A(in_1[0]), .S(out_4[0]), .Cout(main_4_cout));
endmodule
