// Logisim project NORGATE.circ as structural Verilog: 1 circuit, main circuit main
module main (
  input  in_1,
  input  B,
  output Output
);

  wire undriven;

  Pull_Resistor pull_resistor_1 (.node(Output));
  Transistor #(.\type ("n")) transistor_1 (.in(undriven), .out(Output), .gate(in_1));
  Transistor #(.\type ("n")) transistor_2 (.in(undriven), .out(Output), .gate(B));

  // Notes on the sheet:
  //   A
endmodule
