// Logisim project decode.circ as structural Verilog: 1 circuit, main circuit main
module main (
  input  [1:0] in_1,
  output out_2,
  output out_3,
  output out_4,
  output out_5
);

  Decoder #(.enable("false"), .select(2)) decoder_1 (
    .out0(out_2), .out1(out_3), .out2(out_4), .out3(out_5), .sel(in_1));
endmodule
